# Fritzing sketch ControlHeater (saved by Fritzing 0.9.9b)
breadboards: 1

parts:
  Part1 = Arduino Nano (Rev3.0)
  Q1 = Basic FET N-Channel [package="D2Pak [SMD]"]
  LED1 = LED - 3mm [color="Red (633nm)" current=0.030 package="3 mm [THT]"]
  R1 = Resistor [tolerance=±5% power=0.25 resistance=220 package=THT]
  SPKR1 = Loudspeaker  # not connected
  VCC1 = 4 x AAA Battery Mount
  R2 = Resistor [tolerance=±5% power=0.25 resistance=220 package=THT]

nets:
  N1: Part1.GND, Q1.source, LED1.cathode, VCC1.-
  N2: Part1.D3, Q1.Gate, R1.Pin_1
  N3: Q1.drain, VCC1.+, R2.Pin_0, R2.Pin_1
  N4: LED1.anode, R1.Pin_0
