# Fritzing sketch ControlLED (saved by Fritzing 0.9.9b)
breadboards: 1

parts:
  Part1 = Arduino Nano (Rev3.0)
  Q1 = Basic FET N-Channel [package="D2Pak [SMD]"]
  LED1 = LED - 3mm [color="Red (633nm)" current=0.030 package="3 mm [THT]"]
  R1 = Resistor [tolerance=±5% resistance=220 package="1206 [SMD]"]
  R2 = Resistor [tolerance=±5% resistance=220 package="2010 [SMD]"]

nets:
  N1: Part1.GND, Q1.source
  N2: Part1.5V, R2.Pin_1
  N3: Part1.A4, R1.Pin_1
  N4: Q1.Gate, R1.Pin_0
  N5: Q1.drain, LED1.cathode
  N6: LED1.anode, R2.Pin_0
