# Fritzing sketch MAX31856ArduinoNano (saved by Fritzing 0.9.9b)
breadboards: 1

parts:
  Part1 = Arduino Nano (Rev3.0)
  Part2 = Adafruit MAX31856 Thermocouple Amp [part_number="Adafruit #3263"]
  C1 = Ceramic Capacitor [capacitance=100nF voltage=35V package="100 mil [THT, multilayer]"]

nets:
  GND: Part1.GND, Part2.GND
  N1: Part1.D10, Part2.!CS
  N2: Part1.D11/MOSI, Part2.SDI
  N3: Part1.D12/MISO, Part2.SDO
  5V: Part1.5V, Part2.VIN
  N4: Part1.D13/SCK, Part2.SCK
  N5: Part2.THERM+, C1.0
  N6: Part2.THERM-, C1.1

custom parts:
  Adafruit MAX31856 Thermocouple Amp: Thermocouples are very sensitive, requiring a good amplifier with a cold-compensation reference, as well as calculations to handle any non-linearities. For a long time we've suggested our MAX31855K breakout, which works great but is only for K-type thermocouples. Now we're happy to offer a great new thermocouple amplifier/converter that can handle just about any type of thermocouple, and even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
