# Fritzing sketch DRV8833 (saved by Fritzing 0.9.9b)
breadboards: 1

parts:
  Part1 = Arduino Uno (Rev3)
  Part2 = Adafruit DRV8833 DC/Stepper Motor Driver [part_number="Adafruit #3297"]
  Power_plug1 = Power plug
  M1 = DC Motor
  M2 = DC Motor

nets:
  N1: Part1.D10_PWM/SS, Part2.BIN2
  N2: Part1.D11_PWM/MOSI, Part2.BIN1
  GND: Part1.GND, Part2.GND, Power_plug1.GND
  N3: Part1.D2, Part2.!SLEEP
  N4: Part1.D3_PWM, Part2.NFAULT
  N5: Part1.D5_PWM, Part2.AIN1
  N6: Part1.D6_PWM, Part2.AIN2
  N7: Part2.PWRIN, Power_plug1.VCC
  N8: Part2.AOUT2, M1.pin_1
  N9: Part2.AOUT1, M1.pin_2
  N10: Part2.BOUT1, M2.pin_1
  N11: Part2.BOUT2, M2.pin_2

notes:
  Motor A
  Motor B
  5 VDC
  DRV8833

custom parts:
  Adafruit DRV8833 DC/Stepper Motor Driver: Spin two DC motors or step one bi-polar or uni-polar stepper with up to 1.2A per channel using the DRV8833. This motor driver chip is a nice alternative to the TB6612 driver. Like that chip, you get 2 full H-bridges, but this chip is better for low voltage uses (can run from 2.7V up to 10.8V motor power) and has built in current limiting capability. We set it up for 1A current limiting so you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
